# Fritzing sketch PCB (saved by Fritzing 1.0.2b)
circuit board: 8.46667cm x 5.64444cm
breadboards: 1

parts:
  GLCD_128x2 = 128 x 64 Graphic LCD Winstar wdg0151-tmi-V#N00
  A1 = Raspberry Pi Pico H
  R1 = 12mm Trimmer Potentiometer (Large) [maximum_resistance=10kΩ knob_status=50% power=0.5W package=THT]

nets:
  N1: GLCD_128x2.1_CS1, A1.GP0
  N2: GLCD_128x2.2_CS2, A1.GP1
  N3: GLCD_128x2.3_Vss, GLCD_128x2.4_Vdd, GLCD_128x2.19_A(+), A1.VSYS, R1.leg2
  N4: GLCD_128x2.5_Vo, R1.wiper
  N5: GLCD_128x2.6_D/I, A1.GP5
  N6: GLCD_128x2.7_R/W, A1.GP6
  N7: GLCD_128x2.8_E, A1.GP7
  N8: GLCD_128x2.9_BD0, A1.GP8
  N9: GLCD_128x2.10_DB1, A1.GP9
  N10: GLCD_128x2.11_DB2, A1.GP10
  N11: GLCD_128x2.12_DB3, A1.GP11
  N12: GLCD_128x2.13_DB4, A1.GP12
  N13: GLCD_128x2.14_DB5, A1.GP13
  N14: GLCD_128x2.15_DB6, A1.GP14
  N15: GLCD_128x2.16_DB7, A1.GP15
  N16: GLCD_128x2.17_RST, A1.GP16
  N17: GLCD_128x2.18_VEE, R1.leg1
  N18: GLCD_128x2.20_K(-), A1.VBUS

custom parts:
  128 x 64 Graphic LCD Winstar wdg0151-tmi-V#N00: Winstar wdg0151-tmi-V#N00
  Raspberry Pi Pico H: Raspberry Pi Pico H. Based around the RP2040 microcontroller the Pico H is a low cost microcontroller device bringing Raspberry Pi quality, cost, and easy of use to the microcontroller space.
